# Fritzing sketch 10w-rgb-led (saved by Fritzing 0.8.0b)

parts:
  LED1 = LED - 5mm [color="Red (635nm)" package="5 mm [THT]"]
  LED2 = LED - 5mm [color="Red (635nm)" package="5 mm [THT]"]
  LED9 = LED - 5mm [color="Blue (470nm)" package="5 mm [THT]"]
  LED3 = LED - 5mm [color="Red (635nm)" package="5 mm [THT]"]
  LED5 = LED - 5mm [color="Green (560nm)" package="5 mm [THT]"]
  LED7 = LED - 5mm [color="Blue (470nm)" package="5 mm [THT]"]
  LED8 = LED - 5mm [color="Blue (470nm)" package="5 mm [THT]"]
  LED4 = LED - 5mm [color="Green (560nm)" package="5 mm [THT]"]
  J1 = female pin header, 3 pins [form="♀ (female)"]
  J2 = female pin header, 3 pins [form="♀ (female)"]
  LED6 = LED - 5mm [color="Green (560nm)" package="5 mm [THT]"]

nets:
  N1: LED1.cathode, J2.pin1
  N2: LED1.anode, LED2.cathode
  N3: LED2.anode, LED3.cathode
  N4: LED9.cathode, LED8.anode
  N5: LED9.anode, J1.pin3
  N6: LED3.anode, J1.pin1
  N7: LED5.cathode, LED4.anode
  N8: LED5.anode, LED6.cathode
  N9: LED7.cathode, J2.pin3
  N10: LED7.anode, LED8.cathode
  N11: LED4.cathode, J2.pin2
  N12: J1.pin2, LED6.anode
