# Fritzing sketch 9v-led (saved by Fritzing 0.9.0b)

parts:
  LED = LED - 5mm [color="Green (560nm)" package="5 mm [THT]"]
  Power_supply = Battery block 9V
  Resistor = Resistor [tolerance=±5% resistance=330 package=THT]

nets:
  N1: LED.cathode, Power_supply.-
  N2: LED.anode, Resistor.Pin_1
  N3: Power_supply.+, Resistor.Pin_0
