# Fritzing sketch arduino-knob (saved by Fritzing 0.8.3b)

parts:
  R1 = Rotary Potentiometer (Small)
  J1 = Basic Servo
  Bauteil1 = Arduino Mega 2560 (Rev3)

nets:
  VCC: R1.leg1, J1.vcc, Bauteil1.5V
  N1: R1.wiper, Bauteil1.A0
  GND: R1.leg2, J1.gnd, Bauteil1.GND
  N2: J1.pulse, Bauteil1.D13_PWM
