# Fritzing sketch arduino-leds (saved by Fritzing 0.9.0b)

parts:
  Resistor = Resistor [tolerance=±5% resistance=220 package=THT]
  LED1 = LED - 5mm [color="Red (633nm)" package="5 mm [THT]"]
  LED2 = LED - 5mm [color="Red (633nm)" package="5 mm [THT]"]
  Resistor1 = Resistor [tolerance=±5% resistance=220 package=THT]
  part = Resistor [tolerance=±5% resistance=220 package=THT]  # not connected
  Part1 = Arduino Mega 2560 (Rev3)

nets:
  N1: Resistor.Pin_0, LED1.anode
  N2: Resistor.Pin_1, Part1.D13_PWM
  N3: LED1.cathode, Part1.GND
  N4: LED2.cathode, Resistor1.Pin_0
  N5: LED2.anode, Part1.5V
  N6: Resistor1.Pin_1, Part1.D2_PWM
