# Fritzing sketch arduino-mosfet-dc-motor (saved by Fritzing 0.9.0b)

parts:
  M1 = DC Motor
  VCC1 = Battery block 9V
  Q2 = MOSFET-NCHANNEL [package=to220v]
  part = DC Motor  # not connected
  Part1 = Arduino Mega 2560 (Rev3)

nets:
  N1: M1.pin_1, Q2.D
  N2: M1.pin_2, VCC1.+
  N3: VCC1.-, Q2.S, Part1.GND
  N4: Q2.G, Part1.D7_PWM
