# Fritzing sketch arduino-potentiometer-blinking (saved by Fritzing 0.8.0b)

parts:
  R1 = Rotary Potentiometer (Small)
  Bauteil1 = Arduino Mega 2560 (Rev3)

nets:
  N1: R1.leg1, Bauteil1.5V
  N2: R1.wiper, Bauteil1.A0
  N3: R1.leg2, Bauteil1.GND
