# Fritzing sketch arduino-servo (saved by Fritzing 0.8.3b)

parts:
  Part1 = Arduino Mega 2560 (Rev3)
  J1 = Basic Servo

nets:
  5V: Part1.5V, J1.vcc
  GND: Part1.GND, J1.gnd
  N1: Part1.D7_PWM, J1.pulse
