# Fritzing sketch arduino-transistor-power-led (saved by Fritzing 0.8.4b)

parts:
  Part1 = Arduino Mega 2560 (Rev3)
  Q1 = NPN-Transistor [package="TO92 [THT]"]
  VCC1 = Battery block 9V
  R1 = Resistor [tolerance=±5% resistance=1k package=THT]
  LED1 = LED - 5mm [color="Red (633nm)" package="5 mm [THT]"]
  LED2 = LED - 5mm [color="Red (633nm)" package="5 mm [THT]"]
  LED3 = LED - 5mm [color="Red (633nm)" package="5 mm [THT]"]
  R2 = Resistor [tolerance=±5% resistance=220 package=THT]

nets:
  N1: Part1.GND, Q1.C, VCC1.-
  N2: Part1.D7_PWM, R1.Pin_1
  N3: Q1.E, R2.Pin_1
  N4: Q1.B, R1.Pin_0
  N5: VCC1.+, LED3.anode
  N6: LED1.cathode, R2.Pin_0
  N7: LED1.anode, LED2.cathode
  N8: LED2.anode, LED3.cathode
