# Fritzing sketch battery-two-diodes (saved by Fritzing 0.9.0b)

parts:
  VCC1 = Battery block 9V
  part = Battery block 9V  # not connected
  D1 = Diode [package=diode-1n4001]
  D2 = Diode [package=diode-1n4001]

nets:
  N1: VCC1.-, D1.A, D1.C, D2.C
  N2: VCC1.+, D2.A
