# Fritzing sketch bus (saved by Fritzing 0.9.0b)

parts:
  Pin = female pin header, 1 pin [form="♀ (female)"]
  RL = Resistor [tolerance=±5% resistance=10k package=THT]
  R1 = Resistor [tolerance=±20% resistance=10 package=THT]
  RL_2 = Resistor [tolerance=±5% resistance=10k package=THT]
  RL_3 = Resistor [tolerance=±5% resistance=10k package=THT]

nets:
  N1: Pin.pin1, RL.Pin_0, R1.Pin_1, RL_2.Pin_0, RL_3.Pin_0
  GND: RL.Pin_1, RL_2.Pin_1, RL_3.Pin_1
  3.3V: R1.Pin_0
