# Fritzing sketch lcd1602 (saved by Fritzing 0.8.0b)

parts:
  Part2 = Arduino Mega 2560 (Rev3)
  LCD1 = LCD screen
  SELECT = Pushbutton [package=THT]
  S2 = Pushbutton [package=THT]
  UP = Pushbutton [package=THT]
  RIGHT = Pushbutton [package=THT]
  DOWN = Pushbutton [package=THT]
  RESET = Pushbutton [package=THT]
  R2 = Resistor [tolerance=±5% resistance=10k package=THT]
  R3 = Resistor [tolerance=±5% resistance=10k package=THT]
  R5 = Resistor [tolerance=±5% resistance=10k package=THT]
  R6 = Resistor [tolerance=±5% resistance=10k package=THT]
  R4 = Resistor [tolerance=±5% resistance=2.2k package=THT]
  R7 = Rotary Potentiometer (Large) [maximum_resistance=100kΩ package=THT]

nets:
  N1: Part2.A0, RIGHT.leg1, R4.Pin_1
  GND: Part2.GND, LCD1.VSS, SELECT.leg0, S2.leg0, UP.leg0, RIGHT.leg0, DOWN.leg0, RESET.leg0, R7.leg2
  N2: Part2.D10_PWM, LCD1.LED-
  N3: Part2.D9_PWM, LCD1.R/W, LCD1.E
  N4: Part2.D8_PWM, LCD1.RS
  N5: Part2.RESET, RESET.leg1
  5V: Part2.5V, LCD1.VDD, LCD1.V0, LCD1.LED+, R4.Pin_0, R7.leg1, R7.wiper
  N6: Part2.D4_PWM, LCD1.DB3, LCD1.DB4
  N7: Part2.D5_PWM, LCD1.DB5
  N8: Part2.D6_PWM, LCD1.DB6
  N9: Part2.D7_PWM, LCD1.DB7
  N10: SELECT.leg1, R6.Pin_0
  GND_2: S2.leg1, R2.Pin_0, R6.Pin_1
  N11: UP.leg1, R3.Pin_0, R5.Pin_1
  N12: DOWN.leg1, R2.Pin_1, R5.Pin_0
