# Fritzing sketch n-channel-fet (saved by Fritzing 0.9.0b)

parts:
  12V = 4 x AAA Battery Mount
  5V = Battery block 9V
  Switch = Square Pushbutton
  Inductive_load = Inductor [package="400 mil [THT]"]
  Q4 = Basic FET N-Channel [package="DPak [SMD]"]
  part = Zener Diode [part_number=1N4732A breakdown_voltage=3.6V package="300 mil [THT]"]  # not connected

nets:
  GND: 12V.-, 5V.-, Q4.source
  N1: 12V.+, Inductive_load.pin_0
  N2: 5V.+, Switch.leg0
  N3: Switch.leg1, Q4.Gate
  N4: Inductive_load.pin_1, Q4.drain
