# Fritzing sketch npn-transistor (saved by Fritzing 0.8.3b)

parts:
  NPN_transistor = NPN-Transistor [package="TO92 [THT]"]
  Load = Resistor [tolerance=±5% resistance=220 package=THT]
  12V = 4 x AAA Battery Mount
  Rbe = Resistor [tolerance=±5% resistance=220 package=THT]
  5V = Battery block 9V
  Switch = Square Pushbutton

nets:
  GND: NPN_transistor.E, 12V.-, Rbe.Pin_0
  N1: NPN_transistor.B, Switch.leg0
  N2: NPN_transistor.C, Load.Pin_1
  N3: Load.Pin_0, 12V.+
  N4: Rbe.Pin_1, 5V.-
  N5: 5V.+, Switch.leg1

notes:
  Emitter
  Collector
  Base
