# Fritzing sketch pin-high (saved by Fritzing 0.9.0b)

parts:
  Pin = female pin header, 1 pin [form="♀ (female)"]
  R2 = Resistor [tolerance=±5% resistance=1M package=THT]
  part = Resistor [tolerance=±20% resistance=10 package=THT]

nets:
  N1: Pin.pin1, R2.Pin_0, part.Pin_1
  GND: R2.Pin_1
  5V: part.Pin_0
