# Fritzing sketch pin-low (saved by Fritzing 0.9.0b)

parts:
  Pin = female pin header, 1 pin [form="♀ (female)"]
  R1 = Resistor [tolerance=±5% resistance=1M package=THT]
  part = Resistor [tolerance=±5% resistance=10 package=THT]

nets:
  N1: Pin.pin1, R1.Pin_1, part.Pin_0
  5V: R1.Pin_0
  GND: part.Pin_1
