# Fritzing sketch pin-pull-down (saved by Fritzing 0.8.3b)

parts:
  Pin = female pin header, 1 pin [form="♀ (female)"]
  R2 = Resistor [tolerance=±5% resistance=1.5k package=THT]
  R1 = Resistor [tolerance=±5% resistance=1M package=THT]

nets:
  N1: Pin.pin1, R2.Pin_0, R1.Pin_1
  GND: R2.Pin_1
  5V: R1.Pin_0
