# Fritzing sketch pnp-transistor (saved by Fritzing 0.8.3b)

parts:
  PNP_transistor = PNP-Transistor [package="TO92 [THT]"]
  Load = Resistor [tolerance=±5% resistance=220 package=THT]
  12V = 4 x AAA Battery Mount
  5V = Battery block 9V
  Switch = Square Pushbutton
  Reb = Resistor [tolerance=±5% resistance=220 package=THT]

nets:
  N1: PNP_transistor.E, 12V.+, Reb.Pin_0
  N2: PNP_transistor.B, Switch.leg0
  N3: PNP_transistor.C, Load.Pin_0
  GND: Load.Pin_1, 12V.-
  N4: 5V.-, Switch.leg1
  N5: 5V.+, Reb.Pin_1

notes:
  Base
  Collector
  Emitter
