# Fritzing sketch resistance (saved by Fritzing 0.9.0b)

parts:
  Resistor = Resistor [tolerance=±5% resistance=220 package=THT]
  Power_supply = Battery block 9V

nets:
  N1: Resistor.Pin_0, Power_supply.-
  N2: Resistor.Pin_1, Power_supply.+
