# Fritzing sketch transistors (saved by Fritzing 0.8.3b)

parts:
  NPN_transistor = NPN-Transistor [package="TO92 [THT]"]
  PNP_transistor = PNP-Transistor [package="TO92 [THT]"]
  Load = Resistor [tolerance=±5% resistance=220 package=THT]
  Load_2 = Resistor [tolerance=±5% resistance=220 package=THT]
  12V = 4 x AAA Battery Mount
  12V_2 = 4 x AAA Battery Mount

nets:
  N1: NPN_transistor.E, 12V_2.-
  N2: NPN_transistor.C, Load.Pin_1
  N3: PNP_transistor.E, 12V.+
  N4: PNP_transistor.C, Load_2.Pin_0
  N5: Load.Pin_0, 12V_2.+
  N6: Load_2.Pin_1, 12V.-

notes:
  Base
  Collector
  Emitter
