# Fritzing sketch uln2803-rgb-led (saved by Fritzing 0.8.0b)

parts:
  Part1 = Arduino Mega 2560 (Rev3)
  IC1 = ULN2803A [package=THT]
  Power_RGB1 = Prolight RGB 3 Watt Star
  R1 = Resistor [tolerance=±5% resistance=220 package=THT]
  R2 = Resistor [tolerance=±5% resistance=220 package=THT]
  R3 = Resistor [tolerance=±5% resistance=220 package=THT]

nets:
  N1: Part1.GND, IC1.0V
  N2: Part1.VIN, IC1.COM_-_Common, Power_RGB1.B+, Power_RGB1.G+, Power_RGB1.R+
  N3: Part1.D3_PWM, IC1.In_7, IC1.In_8
  N4: Part1.D5_PWM, IC1.In_4, IC1.In_5, IC1.In_6
  N5: Part1.D6_PWM, IC1.In_1, IC1.In_2, IC1.In_3
  N6: IC1.Out_8, IC1.Out_7, R1.Pin_1
  N7: IC1.Out_6, IC1.Out_5, IC1.Out_4, R3.Pin_1
  N8: IC1.Out_3, IC1.Out_2, IC1.Out_1, R2.Pin_1
  N9: Power_RGB1.R-, R1.Pin_0
  N10: Power_RGB1.G-, R3.Pin_0
  N11: Power_RGB1.B-, R2.Pin_0
